// Logisim project main.circ as structural Verilog
module main (
  input  [4:0] RightBatY
);

  wire cdm_8_mark5_1_p1, clock_1_out, R_out;
  wire [4:0] joystick_1_y, kinematic_controller_1_ballx_2, kinematic_controller_1_bally,
       kinematic_controller_1_chipid, kinematic_controller_1_leftbaty, kinematic_controller_1_rightbaty,
       not_1_out, videochip_1_out_14, videochip_1_out_15, videochip_1_out_16, videochip_1_out_17,
       videochip_1_out_18, videochip_2_out_14, videochip_2_out_15, videochip_2_out_16, videochip_2_out_17,
       videochip_2_out_18, videochip_3_out_14, videochip_3_out_15, videochip_3_out_16, videochip_3_out_17,
       videochip_3_out_18;
  wire [31:0] videochip_1_out_6, videochip_1_out_7, videochip_1_out_8, videochip_1_out_9, videochip_1_out_10,
       videochip_1_out_11, videochip_1_out_12, videochip_1_out_13, videochip_2_out_6, videochip_2_out_7,
       videochip_2_out_8, videochip_2_out_9, videochip_2_out_10, videochip_2_out_11, videochip_2_out_12,
       videochip_2_out_13, videochip_3_out_6, videochip_3_out_7, videochip_3_out_8, videochip_3_out_9,
       videochip_3_out_10, videochip_3_out_11, videochip_3_out_12, videochip_3_out_13, videochip_4_out_6,
       videochip_4_out_7, videochip_4_out_8, videochip_4_out_9, videochip_4_out_10, videochip_4_out_11,
       videochip_4_out_12, videochip_4_out_13;

  // CdM_8_mark5 cdm_8_mark5_1: pin names not known; wires that end beside it: cdm_8_mark5_1_p1, cdm_8_mark5_1_p1
  Joystick #(.bits(5)) joystick_1 (.y(joystick_1_y));  // open: x
  assign not_1_out = ~joystick_1_y;  // NOT_Gate not_1, 5 bits wide
  Button R (.out(R_out));
  Videochip videochip_1 (
    .BallX(kinematic_controller_1_ballx_2), .BallY(kinematic_controller_1_bally),
    .LeftBatY(kinematic_controller_1_leftbaty), .RightBatY(kinematic_controller_1_rightbaty),
    .ChipID(kinematic_controller_1_chipid), .out_18(videochip_1_out_18), .out_14(videochip_1_out_14),
    .out_15(videochip_1_out_15), .out_16(videochip_1_out_16), .out_17(videochip_1_out_17),
    .out_6(videochip_1_out_6), .out_8(videochip_1_out_8), .out_9(videochip_1_out_9),
    .out_10(videochip_1_out_10), .out_11(videochip_1_out_11), .out_12(videochip_1_out_12),
    .out_13(videochip_1_out_13), .out_7(videochip_1_out_7));
  DotMatrix #(.matrixcols(32), .matrixrows(32)) dotmatrix_1 (
    .col0(videochip_1_out_6), .col1(videochip_1_out_7), .col2(videochip_1_out_8), .col3(videochip_1_out_9),
    .col4(videochip_1_out_10), .col5(videochip_1_out_11), .col6(videochip_1_out_12),
    .col7(videochip_1_out_13), .col8(videochip_2_out_6), .col9(videochip_2_out_7), .col10(videochip_2_out_8),
    .col11(videochip_2_out_9), .col12(videochip_2_out_10), .col13(videochip_2_out_11),
    .col14(videochip_2_out_12), .col15(videochip_2_out_13), .col16(videochip_3_out_6),
    .col17(videochip_3_out_7), .col18(videochip_3_out_8), .col19(videochip_3_out_9),
    .col20(videochip_3_out_10), .col21(videochip_3_out_11), .col22(videochip_3_out_12),
    .col23(videochip_3_out_13), .col24(videochip_4_out_6), .col25(videochip_4_out_7),
    .col26(videochip_4_out_8), .col27(videochip_4_out_9), .col28(videochip_4_out_10),
    .col29(videochip_4_out_11), .col30(videochip_4_out_12), .col31(videochip_4_out_13));
  Kinematic_Controller kinematic_controller_1 (
    .RightYIn(RightBatY), .BallX_2(kinematic_controller_1_ballx_2), .BallY(kinematic_controller_1_bally),
    .LeftBatY(kinematic_controller_1_leftbaty), .RightBatY(kinematic_controller_1_rightbaty),
    .ChipID(kinematic_controller_1_chipid), .Reset(R_out), .LeftYIn(not_1_out), .Clock(clock_1_out));  // open: BallX, BallY_2, vxy, out_13, out_14
  Clock #(.highDuration(1000), .lowDuration(1000)) clock_1 (.out(clock_1_out));
  Videochip videochip_2 (
    .BallX(videochip_1_out_14), .BallY(videochip_1_out_15), .LeftBatY(videochip_1_out_16),
    .RightBatY(videochip_1_out_17), .ChipID(videochip_1_out_18), .out_18(videochip_2_out_18),
    .out_14(videochip_2_out_14), .out_15(videochip_2_out_15), .out_16(videochip_2_out_16),
    .out_17(videochip_2_out_17), .out_6(videochip_2_out_6), .out_8(videochip_2_out_8),
    .out_9(videochip_2_out_9), .out_10(videochip_2_out_10), .out_11(videochip_2_out_11),
    .out_12(videochip_2_out_12), .out_13(videochip_2_out_13), .out_7(videochip_2_out_7));
  Videochip videochip_3 (
    .BallX(videochip_2_out_14), .BallY(videochip_2_out_15), .LeftBatY(videochip_2_out_16),
    .RightBatY(videochip_2_out_17), .ChipID(videochip_2_out_18), .out_18(videochip_3_out_18),
    .out_14(videochip_3_out_14), .out_15(videochip_3_out_15), .out_16(videochip_3_out_16),
    .out_17(videochip_3_out_17), .out_6(videochip_3_out_6), .out_8(videochip_3_out_8),
    .out_9(videochip_3_out_9), .out_10(videochip_3_out_10), .out_11(videochip_3_out_11),
    .out_12(videochip_3_out_12), .out_13(videochip_3_out_13), .out_7(videochip_3_out_7));
  Videochip videochip_4 (
    .BallX(videochip_3_out_14), .BallY(videochip_3_out_15), .LeftBatY(videochip_3_out_16),
    .RightBatY(videochip_3_out_17), .ChipID(videochip_3_out_18), .out_6(videochip_4_out_6),
    .out_8(videochip_4_out_8), .out_9(videochip_4_out_9), .out_10(videochip_4_out_10),
    .out_11(videochip_4_out_11), .out_12(videochip_4_out_12), .out_13(videochip_4_out_13),
    .out_7(videochip_4_out_7));  // open: out_18, out_14, out_15, out_16, out_17

  // Notes on the sheet:
  //   Менің Бағдарламам
endmodule

module Videochip (
  input  [4:0] BallX,
  input  [4:0] BallY,
  input  [4:0] LeftBatY,
  input  [4:0] RightBatY,
  input  [4:0] ChipID,
  output [31:0] out_6,
  output [31:0] out_7,
  output [31:0] out_8,
  output [31:0] out_9,
  output [31:0] out_10,
  output [31:0] out_11,
  output [31:0] out_12,
  output [31:0] out_13,
  output [4:0] out_14,
  output [4:0] out_15,
  output [4:0] out_16,
  output [4:0] out_17,
  output [4:0] out_18
);

  wire [31:0] ball_4_out_5, ball_5_out_5, bat_1_out_5, bat_2_out_5;

  Ball ball_1 (.BallX(BallX), .BallY(BallY), .NumColumn({5{1'b0}}), .ChipID(ChipID), .out_5(out_6));
  Ball ball_2 (.BallX(BallX), .BallY(BallY), .NumColumn(5'b00001), .ChipID(ChipID), .out_5(out_7));
  Ball ball_3 (.BallX(BallX), .BallY(BallY), .NumColumn(5'b00010), .ChipID(ChipID), .out_5(out_8));
  assign out_9 = bat_1_out_5 | ball_4_out_5;  // OR_Gate or_1, 32 bits wide
  Bat bat_1 (.BatX(5'b00011), .BatY(LeftBatY), .NumColumn(5'b00011), .ChipID(ChipID), .out_5(bat_1_out_5));
  Ball ball_4 (.BallX(BallX), .BallY(BallY), .NumColumn(5'b00011), .ChipID(ChipID), .out_5(ball_4_out_5));
  Adder #(.width(5)) adder_1 (.a(ChipID), .b(5'b00001), .out(out_18));  // open: cin, cout
  assign out_10 = bat_2_out_5 | ball_5_out_5;  // OR_Gate or_2, 32 bits wide
  Bat bat_2 (.BatX(5'b11100), .BatY(RightBatY), .NumColumn(5'b00100), .ChipID(ChipID), .out_5(bat_2_out_5));
  Ball ball_5 (.BallX(BallX), .BallY(BallY), .NumColumn(5'b00100), .ChipID(ChipID), .out_5(ball_5_out_5));
  Ball ball_6 (.BallX(BallX), .BallY(BallY), .NumColumn(5'b00101), .ChipID(ChipID), .out_5(out_11));
  Ball ball_7 (.BallX(BallX), .BallY(BallY), .NumColumn(5'b00110), .ChipID(ChipID), .out_5(out_12));
  Ball ball_8 (.BallX(BallX), .BallY(BallY), .NumColumn(5'b00111), .ChipID(ChipID), .out_5(out_13));

  assign out_14 = BallX;
  assign out_15 = BallY;
  assign out_16 = LeftBatY;
  assign out_17 = RightBatY;
endmodule

module Bat (
  input  [4:0] BatX,
  input  [4:0] BatY,
  input  [4:0] NumColumn,
  input  [4:0] ChipID,
  output [31:0] out_5
);

  wire comparator_1_eq;
  wire [4:0] adder_1_out, multiplier_1_out;
  wire [31:0] decoder_1_out0, or_1_out, shifter_1_out, shifter_2_out;

  Decoder #(.select(5), .disabled(0)) decoder_1 (
    .out0(decoder_1_out0[0]), .out1(decoder_1_out0[1]), .out2(decoder_1_out0[2]), .out3(decoder_1_out0[3]),
    .out4(decoder_1_out0[4]), .out5(decoder_1_out0[5]), .out6(decoder_1_out0[6]), .out7(decoder_1_out0[7]),
    .out8(decoder_1_out0[8]), .out9(decoder_1_out0[9]), .out10(decoder_1_out0[10]),
    .out11(decoder_1_out0[11]), .out12(decoder_1_out0[12]), .out13(decoder_1_out0[13]),
    .out14(decoder_1_out0[14]), .out15(decoder_1_out0[15]), .out16(decoder_1_out0[16]),
    .out17(decoder_1_out0[17]), .out18(decoder_1_out0[18]), .out19(decoder_1_out0[19]),
    .out20(decoder_1_out0[20]), .out21(decoder_1_out0[21]), .out22(decoder_1_out0[22]),
    .out23(decoder_1_out0[23]), .out24(decoder_1_out0[24]), .out25(decoder_1_out0[25]),
    .out26(decoder_1_out0[26]), .out27(decoder_1_out0[27]), .out28(decoder_1_out0[28]),
    .out29(decoder_1_out0[29]), .out30(decoder_1_out0[30]), .out31(decoder_1_out0[31]), .sel(BatY));  // open: en
  Multiplier #(.width(5)) multiplier_1 (.a(ChipID), .b(5'b01000), .out(multiplier_1_out));  // open: cin, cout
  Shifter #(.width(32)) shifter_1 (.in(decoder_1_out0), .\dist (5'b00001), .out(shifter_1_out));
  Shifter #(.width(32)) shifter_2 (.in(decoder_1_out0), .\dist (5'b00010), .out(shifter_2_out));
  Adder #(.width(5)) adder_1 (.a(NumColumn), .b(multiplier_1_out), .out(adder_1_out));  // open: cin, cout
  assign or_1_out = shifter_1_out | decoder_1_out0 | shifter_2_out;  // OR_Gate or_1, 32 bits wide
  Comparator #(.width(5), .mode("unsigned")) comparator_1 (
    .a(BatX), .b(adder_1_out), .eq(comparator_1_eq));  // open: gt, lt
  Multiplexer #(.width(32), .disabled(0), .enable("false")) multiplexer_1 (
    .in0({32{1'b0}}), .in1(or_1_out), .out(out_5), .sel(comparator_1_eq));
endmodule

module Ball (
  input  [4:0] BallX,
  input  [4:0] BallY,
  input  [4:0] NumColumn,
  input  [4:0] ChipID,
  output [31:0] out_5
);

  wire comparator_1_eq;
  wire [4:0] adder_1_out, multiplier_1_out;
  wire [31:0] decoder_1_out0;

  Decoder #(.select(5), .disabled(0)) decoder_1 (
    .out0(decoder_1_out0[0]), .out1(decoder_1_out0[1]), .out2(decoder_1_out0[2]), .out3(decoder_1_out0[3]),
    .out4(decoder_1_out0[4]), .out5(decoder_1_out0[5]), .out6(decoder_1_out0[6]), .out7(decoder_1_out0[7]),
    .out8(decoder_1_out0[8]), .out9(decoder_1_out0[9]), .out10(decoder_1_out0[10]),
    .out11(decoder_1_out0[11]), .out12(decoder_1_out0[12]), .out13(decoder_1_out0[13]),
    .out14(decoder_1_out0[14]), .out15(decoder_1_out0[15]), .out16(decoder_1_out0[16]),
    .out17(decoder_1_out0[17]), .out18(decoder_1_out0[18]), .out19(decoder_1_out0[19]),
    .out20(decoder_1_out0[20]), .out21(decoder_1_out0[21]), .out22(decoder_1_out0[22]),
    .out23(decoder_1_out0[23]), .out24(decoder_1_out0[24]), .out25(decoder_1_out0[25]),
    .out26(decoder_1_out0[26]), .out27(decoder_1_out0[27]), .out28(decoder_1_out0[28]),
    .out29(decoder_1_out0[29]), .out30(decoder_1_out0[30]), .out31(decoder_1_out0[31]), .sel(BallY));  // open: en
  Multiplier #(.width(5)) multiplier_1 (.a(ChipID), .b(5'b01000), .out(multiplier_1_out));  // open: cin, cout
  Adder #(.width(5)) adder_1 (.a(NumColumn), .b(multiplier_1_out), .out(adder_1_out));  // open: cin, cout
  Comparator #(.width(5), .mode("unsigned")) comparator_1 (
    .a(BallX), .b(adder_1_out), .eq(comparator_1_eq));  // open: gt, lt
  Multiplexer #(.width(32), .disabled(0), .enable("false")) multiplexer_1 (
    .in0({32{1'b0}}), .in1(decoder_1_out0), .out(out_5), .sel(comparator_1_eq));
endmodule

module Kinematic_Controller (
  input  Reset,
  input  [4:0] LeftYIn,
  input  [4:0] RightYIn,
  input  Clock,
  output [7:0] BallX,
  output [4:0] BallX_2,
  output [4:0] BallY,
  output [7:0] BallY_2,
  output [4:0] LeftBatY,
  output [4:0] RightBatY,
  output [4:0] ChipID,
  output [7:0] vxy,
  output [7:0] out_13,
  output [7:0] out_14
);

  wire adder_3_cout, adder_4_cout, adder_7_cout, adder_8_cout, Bcontact, comparator_1_eq, comparator_2_eq,
       comparator_3_eq, comparator_4_eq, hitA, hitB, inrange_1_sharearow, inrange_2_sharearow, LBcontact,
       not_1_out, not_4_out, not_5_out, RBcontact, reset_t, vxrefl, vyrefl;
  wire [2:0] vx;
  wire [4:0] x, y;
  wire [5:3] vxy_t;
  wire [7:0] adder_1_out, adder_2_out, adder_5_out, adder_6_out, bit_extender_3_out, bit_extender_4_out,
       longVX, longVY, multiplexer_1_out, multiplexer_2_out, shifter_1_out, shifter_2_out, vxreg, vyreg,
       xreg, yreg;

  or or_1 (reset_t, Reset, Bcontact);
  Adder adder_1 (.a(xreg), .b(vxreg), .out(adder_1_out));  // open: cin, cout
  Multiplexer #(.width(8), .disabled(0), .enable("false")) multiplexer_1 (
    .in0(adder_1_out), .in1(8'h80), .out(multiplexer_1_out), .sel(reset_t));
  Adder adder_2 (.a(yreg), .b(vyreg), .out(adder_2_out));  // open: cin, cout
  Multiplexer #(.width(8), .disabled(0), .enable("false")) multiplexer_2 (
    .in0(adder_2_out), .in1(8'h80), .out(multiplexer_2_out), .sel(reset_t));
  Shifter #(.shift("lr")) shifter_1 (.in(xreg), .\dist (3'b011), .out(shifter_1_out));
  Shifter #(.shift("lr")) shifter_2 (.in(yreg), .\dist (3'b011), .out(shifter_2_out));
  Register register_1 (.D(multiplexer_1_out), .Q(xreg), .clk(Clock));  // open: en, clr
  Register register_2 (.D(multiplexer_2_out), .Q(yreg), .clk(Clock));  // open: en, clr
  Bit_Extender #(.out_width(5)) bit_extender_1 (.in(shifter_1_out), .out(x));
  Bit_Extender #(.out_width(5)) bit_extender_2 (.in(shifter_2_out), .out(y));
  assign bit_extender_3_out = {{5{1'b0}}, vx};  // Bit_Extender bit_extender_3
  assign bit_extender_4_out = {{5{1'b0}}, vxy_t};  // Bit_Extender bit_extender_4
  Adder adder_3 (.a(xreg), .b(longVX), .cout(adder_3_cout));  // open: out, cin
  Adder adder_4 (.a(yreg), .b(longVY), .cout(adder_4_cout));  // open: out, cin
  Shifter shifter_3 (.in(bit_extender_3_out), .\dist (3'b101), .out(longVX));
  Shifter shifter_4 (.in(bit_extender_4_out), .\dist (3'b101), .out(longVY));
  Comparator #(.width(1), .mode("unsigned")) comparator_1 (
    .a(longVX[7]), .b(adder_3_cout), .eq(comparator_1_eq));  // open: gt, lt
  Comparator #(.width(1), .mode("unsigned")) comparator_2 (
    .a(longVY[7]), .b(adder_4_cout), .eq(comparator_2_eq));  // open: gt, lt
  not not_1 (not_1_out, longVX[7]);
  // Probe on longVX
  // Probe on longVY
  not not_2 (vxrefl, comparator_1_eq);
  not not_3 (vyrefl, comparator_2_eq);
  and and_1 (hitA, vxrefl, longVX[7]);
  and and_2 (hitB, vxrefl, not_1_out);
  Adder adder_5 (.a(xreg), .b(8'he4), .out(adder_5_out));  // open: cin, cout
  Adder adder_6 (.a(xreg), .b(8'h1c), .out(adder_6_out));  // open: cin, cout
  Adder adder_7 (.a(adder_5_out), .b(longVX), .cout(adder_7_cout));  // open: out, cin
  Adder adder_8 (.a(adder_6_out), .b(longVX), .cout(adder_8_cout));  // open: out, cin
  Comparator #(.width(1), .mode("unsigned")) comparator_3 (
    .a(adder_7_cout), .b(longVX[7]), .eq(comparator_3_eq));  // open: gt, lt
  Comparator #(.width(1), .mode("unsigned")) comparator_4 (
    .a(adder_8_cout), .b(longVX[7]), .eq(comparator_4_eq));  // open: gt, lt
  not not_4 (not_4_out, comparator_3_eq);
  inrange inrange_1 (.YBall(y), .YBat(LeftYIn), .shareArow(inrange_1_sharearow));
  not not_5 (not_5_out, comparator_4_eq);
  inrange inrange_2 (.YBall(y), .YBat(RightYIn), .shareArow(inrange_2_sharearow));
  and and_3 (LBcontact, not_4_out, inrange_1_sharearow);
  and and_4 (RBcontact, not_5_out, inrange_2_sharearow);
  or or_2 (Bcontact, LBcontact, RBcontact);

  assign BallX = {8{1'b0}};
  assign BallX_2 = {5{1'b0}};
  assign BallY = {5{1'b0}};
  assign BallY_2 = {8{1'b0}};
  assign ChipID = {5{1'b0}};
  assign LeftBatY = LeftYIn;
  assign out_13 = {8{1'b0}};
  assign out_14 = {8{1'b0}};
  assign RightBatY = RightYIn;
  assign vxy = {8{1'b0}};

  // Other names for the same wires on the sheet: vxneg = longVX[7]; vyneg = longVY[7]; R = Reset; vxy_t[2:0] = vx;
  //   vy[2:0] = vxy_t
endmodule

module reflect (
  input  [2:0] oldv,
  output [2:0] newv
);

  wire comparator_1_eq;
  wire [2:0] adder_1_out, not_1_out;

  Comparator #(.width(3), .mode("unsigned")) comparator_1 (.a(oldv), .b(3'b100), .eq(comparator_1_eq));  // open: gt, lt
  not not_1 (not_1_out[0], oldv[0]);
  not not_2 (not_1_out[1], oldv[1]);
  not not_3 (not_1_out[2], oldv[2]);
  Adder #(.width(3)) adder_1 (.a(not_1_out), .b(3'b001), .out(adder_1_out));  // open: cin, cout
  Multiplexer #(.width(3), .disabled(0), .enable("false")) multiplexer_1 (
    .in0(adder_1_out), .in1(not_1_out), .out(newv), .sel(comparator_1_eq));
endmodule

module inrange (
  input  [4:0] YBall,
  input  [4:0] YBat,
  output shareArow
);

  wire comparator_1_eq, comparator_2_eq, comparator_3_eq;
  wire [4:0] adder_1_out, adder_2_out;

  Adder #(.width(5)) adder_1 (.a(YBat), .b(5'b00001), .out(adder_1_out));  // open: cin, cout
  Adder #(.width(5)) adder_2 (.a(adder_1_out), .b(5'b00001), .out(adder_2_out));  // open: cin, cout
  Comparator #(.width(5), .mode("unsigned")) comparator_1 (.a(YBat), .b(YBall), .eq(comparator_1_eq));  // open: gt, lt
  Comparator #(.width(5), .mode("unsigned")) comparator_2 (
    .a(adder_1_out), .b(YBall), .eq(comparator_2_eq));  // open: gt, lt
  Comparator #(.width(5), .mode("unsigned")) comparator_3 (
    .a(adder_2_out), .b(YBall), .eq(comparator_3_eq));  // open: gt, lt
  or or_1 (shareArow, comparator_1_eq, comparator_2_eq, comparator_3_eq);
endmodule
